// Digital circuit 2_12_d.dig as structural Verilog
module _2_12_d (
  input  A,
  input  B,
  input  C,
  input  D,
  output Y
);

  wire nand_1_out, nand_2_out, not_1_out, not_2_out, not_3_out;

  not not_1 (not_1_out, A);
  not not_2 (not_2_out, B);
  not not_3 (not_3_out, D);
  nand nand_1 (nand_1_out, not_1_out, C);
  nand nand_2 (nand_2_out, not_2_out, not_3_out);
  nand nand_3 (Y, nand_1_out, nand_2_out);
endmodule
