// Digital circuit 2_12_e.dig as structural Verilog
module _2_12_e (
  input  A,
  input  B,
  input  C,
  input  D,
  output Y
);

  wire nand_1_out, nand_2_out, nand_3_out, not_1_out, not_2_out;

  not not_1 (not_1_out, A);
  not not_2 (not_2_out, B);
  nand nand_1 (nand_1_out, not_1_out, B, C);
  nand nand_2 (nand_2_out, A, not_2_out);
  nand nand_3 (nand_3_out, not_2_out, C, D);
  nand nand_4 (Y, nand_1_out, nand_2_out, nand_3_out);
endmodule
