// Digital circuit 2_7_a.dig as structural Verilog
module _2_7_a (
  input  A,
  input  B,
  output Y
);

  wire not_1_out;

  not not_1 (not_1_out, B);
  or or_1 (Y, A, not_1_out);

  // Notes on the sheet:
  //   A+!B
endmodule
