// Digital circuit 2_7_b.dig as structural Verilog
module _2_7_b (
  input  A,
  input  B,
  input  C,
  output Y
);

  wire and_1_out, and_2_out, not_1_out, not_2_out, not_3_out;

  and and_1 (and_1_out, A, B, C);
  not not_1 (not_1_out, A);
  not not_2 (not_2_out, B);
  not not_3 (not_3_out, C);
  and and_2 (and_2_out, not_1_out, not_2_out, not_3_out);
  or or_1 (Y, and_1_out, and_2_out);

  // Notes on the sheet:
  //   !a!b!c+abc
endmodule
