// Digital circuit 2_8_b.dig as structural Verilog
module _2_8_b (
  input  A,
  input  B,
  input  C,
  output Y
);

  wire and_1_out, and_2_out, and_3_out, not_1_out, not_2_out;

  not not_1 (not_1_out, A);
  not not_2 (not_2_out, C);
  and and_1 (and_1_out, not_1_out, C);
  and and_2 (and_2_out, A, not_2_out);
  and and_3 (and_3_out, B, not_2_out);
  or or_1 (Y, and_1_out, and_2_out, and_3_out);
endmodule
