// Digital circuit 2_8_c.dig as structural Verilog
module _2_8_c (
  input  A,
  input  B,
  input  C,
  output Y
);

  wire and_1_out, and_2_out, not_1_out, not_2_out;

  not not_1 (not_1_out, A);
  not not_2 (not_2_out, B);
  and and_1 (and_1_out, not_1_out, not_2_out, C);
  and and_2 (and_2_out, A, B);
  or or_1 (Y, and_1_out, and_2_out);
endmodule
