// Digital circuit 2_8_d.dig as structural Verilog
module _2_8_d (
  input  A,
  input  B,
  input  C,
  input  D,
  output Y
);

  wire and_1_out, and_2_out, not_1_out, not_2_out, not_3_out;

  not not_1 (not_1_out, A);
  not not_2 (not_2_out, B);
  not not_3 (not_3_out, D);
  and and_1 (and_1_out, not_1_out, C);
  and and_2 (and_2_out, not_2_out, not_3_out);
  or or_1 (Y, and_1_out, and_2_out);
endmodule
