// Digital circuit 2_8_e.dig as structural Verilog
module _2_8_e (
  input  A,
  input  B,
  input  C,
  input  D,
  output Y
);

  wire and_1_out, and_2_out, and_3_out, not_1_out, not_2_out;

  not not_1 (not_1_out, A);
  not not_2 (not_2_out, B);
  and and_1 (and_1_out, not_1_out, B, C);
  and and_2 (and_2_out, A, not_2_out);
  and and_3 (and_3_out, not_2_out, C, D);
  or or_1 (Y, and_1_out, and_2_out, and_3_out);
endmodule
